# Fritzing sketch Esdrasino (saved by Fritzing 0.9.2b)
circuit board: 7.00059cm x 6.03449cm
breadboards: 1

parts:
  U1 = Voltage Regulator - 5V [package="TO220 [THT]"]
  C2 = Electrolytic Capacitor [capacitance=1µF package="100 mil [THT, electrolytic]"]
  RESET = Pushbutton [package="[THT]"]
  C3 = Ceramic Capacitor [capacitance=100nF package="200 mil [THT, multilayer]"]
  R1 = Resistor [tolerance=±5% resistance=1k package=THT]
  C4 = Ceramic Capacitor [capacitance=100nF package="200 mil [THT, multilayer]"]
  C1 = Electrolytic Capacitor [capacitance=1µF voltage=10V package="100 mil [THT, electrolytic]"]
  XTAL1 = Crystal [frequency="16 Mhz" package=THT]
  LED1 = LED - 5mm [color="Red (633nm)" package="5 mm [THT]"]
  R2 = Resistor [tolerance=±5% resistance=220 package=THT]
  USB = male pin header, 6 pins [form="♂ (male)"]
  IOD0 = female pin header, 8 pins [form="♀ (female)"]
  IOD1 = female pin header, 8 pins [form="♀ (female)"]
  PWD = Power plug
  IOA = female pin header, 6 pins [form="♀ (female)"]
  U2 = atmega168 [package=dip]
  IOP = female pin header, 8 pins [form="♀ (female)"]

nets:
  N1: U1.input_voltage, C1.+, PWD.VCC
  GND: U1.GND, C2.-, RESET.Pin_3, RESET.Pin_4, C3.1, C4.0, C1.-, LED1.cathode, USB.pin5, USB.pin6, IOD1.pin7, PWD.GND, U2.GND, IOP.pin2, IOP.pin3
  5V: U1.output_voltage, C2.+, R1.Pin_0, R2.Pin_1, USB.pin4, U2.VCC, U2.AVCC, U2.AREF, IOP.pin4
  N2: RESET.Pin_1, RESET.Pin_2, R1.Pin_1, U2.RESET, IOP.pin6
  N3: C3.0, XTAL1.pin_1, U2.XLAT2
  N4: C4.1, XTAL1.pin_0, U2.XLAT1
  N5: LED1.anode, R2.Pin_0
  N6: USB.pin2, IOD0.pin2, U2.D1_(TX)
  N7: USB.pin3, IOD0.pin1, U2.D0_(RX)
  N8: IOD0.pin3, U2.D2
  N9: IOD0.pin4, U2.D3_(PWM)
  N10: IOD0.pin5, U2.D4
  N11: IOD0.pin6, U2.D5_(PWM)
  N12: IOD0.pin7, U2.D6_(PWM)
  N13: IOD0.pin8, U2.D7
  N14: IOD1.pin1, U2.D8
  N15: IOD1.pin2, U2.D9_(PWM)
  N16: IOD1.pin3, U2.D10_(PWM)
  N17: IOD1.pin4, U2.D11_(PWM)
  N18: IOD1.pin5, U2.D12
  N19: IOD1.pin6, U2.D13
  N20: IOA.pin1, U2.A0
  N21: IOA.pin2, U2.A1
  N22: IOA.pin3, U2.A2
  N23: IOA.pin4, U2.A3
  N24: IOA.pin5, U2.A4
  N25: IOA.pin6, U2.A5

notes:
  Esdrasino v0.1
  RX←0
  TX←1
  2
  ~3
  4
  ~5
  ~6
  7
  8
  ~9
  ~10
  ~11
  12
  13
  GND
  DIGITAL
  ANALOG IN
  POWER
  RESET
  USB
  1K
  220
  16Mhz
  100nF
  10V/1uF
  ON
  5V
  5
  3
  1
  0
  RST
  ←
  github.com/esdrasedu/esdrasino
